# Fritzing sketch Midimalism (saved by Fritzing 0.9.3b)
circuit board: 4.9cm x 4.9cm
breadboards: 1

parts:
  R33 = Resistor [tolerance=±5% resistance=1k package=THT]
  fuse = Resettable Fuse PTC [package=ptc]
  R34 = Resistor [tolerance=±5% resistance=68 package=THT]
  R35 = Resistor [tolerance=±5% resistance=68 package=THT]
  D17 = Zener Diode [part_number=1N4732A breakdown_voltage=3.3V package="300 mil [THT]"]
  D18 = Zener Diode [part_number=1N4732A breakdown_voltage=3.3V package="300 mil [THT]"]
  ATtiny93 = attiny85 [package=dip]
  R36 = Resistor [tolerance=±5% resistance=1.5k package=THT]
  USB5 = USB+SHIELD [package=usb-b-pth]
  R38 = Rotary Potentiometer (Small) [maximum_resistance=100kΩ package=THT]
  R37 = Rotary Potentiometer (Small) [maximum_resistance=100kΩ package=THT]
  S27 = Momentary Switch [package=tactile-pth]
  S39 = SWITCH-MOMENTARY-2 [package=tactile-pth-12mm]
  S40 = SWITCH-MOMENTARY-2 [package=tactile-pth-12mm]
  S25 = Momentary Switch [package=tactile-pth]
  INPUT = AUDIO-JACK2_multicolor_2holestress [package="audio-jack (multicolor)"]
  LED9 = LED - 5mm [color="Red (633nm)" package="5 mm [THT]"]
  SJ3 = Solder Jumper [package=sj_2s-no]

nets:
  N1: R33.Pin_0, LED9.anode
  N2: R33.Pin_1, fuse.2, ATtiny93.Pin_8, R36.Pin_1, R38.leg2, R37.leg2, INPUT.TIP, INPUT.TSH
  N3: fuse.1, USB5.VBUS
  N4: R34.Pin_0, D17.cathode, USB5.D+
  N5: R34.Pin_1, ATtiny93.Pin_2
  N6: R35.Pin_0, D18.cathode, R36.Pin_0, USB5.D-
  N7: R35.Pin_1, ATtiny93.Pin_1
  N8: D17.anode, D18.anode, ATtiny93.Pin_4, USB5.GND, R38.leg1, R37.leg1, S27.3, S27.4, S39.1, S40.1, S25.3, S25.4, INPUT.SLEEVE, LED9.cathode
  N9: ATtiny93.Pin_3, R38.wiper
  N10: ATtiny93.Pin_5, S40.2, S25.1, S25.2
  N11: ATtiny93.Pin_6, S27.1, S27.2, S39.2
  N12: ATtiny93.Pin_7, INPUT.RING, SJ3.1
  N13: USB5.P$1, USB5.P$2
  N14: R37.wiper, INPUT.RSH, SJ3.2

notes:
  based on Cocomake7
  5V GND
  based on the Cocomake7
  D0 D1 D2 D4
  A1 A2.
  USB

custom parts:
  AUDIO-JACK2_multicolor_2holestress: Stereo audio jack with bypass switches.
